# Fritzing sketch EnvSensingRev1 (saved by Fritzing 0.9.4)
breadboards: 1

parts:
  Part2 = Adafruit_BMP280
  U1 = LIPO-2000mAh [package=lipo-2000]  # not connected
  Part3 = Arduino MKR WiFi 1010

nets:
  VIN: Part2.VIN, Part3.5V

custom parts:
  Adafruit_BMP280: Bosch has stepped up their game with their new BMP280 sensor, an environmental sensor with temperature, barometric pressure that is the next generation upgrade to the BMP085/BMP180/BMP183. This sensor is great for all sorts of weather sensing and can even be used in both I2C and SPI! This precision sensor from Bosch is the best low-cost, precision sensing solution for measuring barometric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
  Arduino MKR WiFi 1010: This is the newest version of the MKR 1000 WIFI, but with an ESP32 module on board made by U-BLOX.
